# Fritzing sketch wiring (saved by Fritzing 0.9.3b)

parts:
  Raspberry_Pi = Raspberry Pi 3 [part_number=RPI-3-V1.2]
  Up = DUO LED RG [package="5 mm [THT]"]
  Right = DUO LED RG [package="5 mm [THT]"]
  Left = DUO LED RG [package="5 mm [THT]"]
  Blue = Basic Servo
  Red = Basic Servo
  Blue_Lock = Basic Servo
  Red_Lock = Basic Servo
  V1 = DC Power [voltage=5]
  Blue_2 = Round Pushbutton
  Red_2 = Round Pushbutton
  Green = Round Pushbutton
  Red_Detect = SWITCH-MOMENTARY-2 [package=tactile-switch-1101ne]
  Blue_Detect = SWITCH-MOMENTARY-2 [package=tactile-switch-1101ne]
  Part1 = RFID-RC522-v2
  10KΩ = 10 kΩ Resistor [package="0603 [SMD]"]
  10KΩ_2 = 10 kΩ Resistor [package="0603 [SMD]"]
  10KΩ_3 = 10 kΩ Resistor [package="0603 [SMD]"]
  10KΩ_4 = 10 kΩ Resistor [package="0603 [SMD]"]
  10KΩ_5 = 10 kΩ Resistor [package="0603 [SMD]"]

nets:
  3V3: Raspberry_Pi.3v3, Raspberry_Pi.3V3, Part1.3.3V
  N1: Raspberry_Pi.GPIO3, Blue_Lock.pulse
  N2: Raspberry_Pi.GIPO4, Red_Lock.pulse
  N3: Raspberry_Pi.GIPO27, 10KΩ_3.Pin_1
  N4: Raspberry_Pi.GIPO22, 10KΩ_4.Pin_1
  N5: Raspberry_Pi.GIPO10, Part1.MOSI
  N6: Raspberry_Pi.GIPO9, Part1.MISO
  N7: Raspberry_Pi.GIPO11, Part1.SCK
  GND: Raspberry_Pi.GND, Up.common_cathode, Right.common_cathode, Left.common_cathode, Blue.gnd, Red.gnd, Blue_Lock.gnd, Red_Lock.gnd, V1.V-, Red_Detect.1, Blue_Detect.1, Part1.GND, 10KΩ.Pin_1, 10KΩ_2.Pin_1, 10KΩ_5.Pin_1
  N8: Raspberry_Pi.GIPO5, Up.red_anode
  N9: Raspberry_Pi.GIPO6, Up.green_anode
  N10: Raspberry_Pi.GIPO13, Right.red_anode
  N11: Raspberry_Pi.GIPO19, Right.green_anode
  N12: Raspberry_Pi.GIPO26, Left.red_anode
  N13: Raspberry_Pi.GIPO21, Blue_2.leg1
  N14: Raspberry_Pi.GIPO20, Red_2.leg1
  N15: Raspberry_Pi.GIPO16, Green.leg1
  N16: Raspberry_Pi.GIPO12, Left.green_anode
  N17: Raspberry_Pi.GIPO8, Part1.SDA
  N18: Raspberry_Pi.GIPO25, Part1.IRQ, Part1.RST
  N19: Raspberry_Pi.GIPO24, Blue.pulse
  N20: Raspberry_Pi.GIPO23, Red.pulse
  VCC: Raspberry_Pi.5V, Blue.vcc, Red.vcc, Blue_Lock.vcc, Red_Lock.vcc, V1.V+
  N21: Blue_2.leg0, 10KΩ.Pin_0
  N22: Red_2.leg0, 10KΩ_2.Pin_0
  N23: Green.leg0, 10KΩ_5.Pin_0
  N24: Red_Detect.2, 10KΩ_3.Pin_0
  N25: Blue_Detect.2, 10KΩ_4.Pin_0

custom parts:
  RFID-RC522-v2: A simple China made RFID-RC522 Reader; do check the pin labels, as this is a MFRC522 based clone.
  10 kΩ Resistor: A generic resistor
